# Fritzing sketch Schaltplan (saved by Fritzing 0.9.4)

parts:
  S1_HOCH = Pushbutton [package=THT]
  S6_VORWAERTS = Pushbutton [package=THT]
  S5_ZURUECK = Pushbutton [package=THT]
  S4_RECHTS = Pushbutton [package=THT]
  S2_RUNTER = Pushbutton [package=THT]
  S3_LINKS = Pushbutton [package=THT]
  Raspberry_Pi_1 = Raspberry Pi 3 [part_number=RPI-3-V1.2]
  4_Channel_Relay1 = 4 Channel Power Relay
  4_Channel_Relay2 = 4 Channel Power Relay
  D1 = Zener Diode [part_number=1N4732A breakdown_voltage=3.6V package="300 mil [THT]"]
  D2 = Zener Diode [part_number=1N4732A breakdown_voltage=3.6V package="300 mil [THT]"]
  D3 = Zener Diode [part_number=1N4732A breakdown_voltage=3.6V package="300 mil [THT]"]
  D4 = Zener Diode [part_number=1N4732A breakdown_voltage=3.6V package="300 mil [THT]"]
  D5 = Zener Diode [part_number=1N4732A breakdown_voltage=3.6V package="300 mil [THT]"]
  D6 = Zener Diode [part_number=1N4732A breakdown_voltage=3.6V package="300 mil [THT]"]
  D7 = Zener Diode [part_number=1N4732A breakdown_voltage=3.6V package="300 mil [THT]"]

nets:
  GND: S1_HOCH.leg0, S6_VORWAERTS.leg0, S5_ZURUECK.leg0, S4_RECHTS.leg0, S2_RUNTER.leg0, S3_LINKS.leg0, Raspberry_Pi_1.GND, 4_Channel_Relay1.GND, 4_Channel_Relay2.GND
  N1: S1_HOCH.leg1, Raspberry_Pi_1.GIPO26
  N2: S6_VORWAERTS.leg1, Raspberry_Pi_1.GPIO2
  N3: S5_ZURUECK.leg1, Raspberry_Pi_1.GIPO21
  N4: S4_RECHTS.leg1, Raspberry_Pi_1.GIPO4
  N5: S2_RUNTER.leg1, Raspberry_Pi_1.GIPO19
  N6: S3_LINKS.leg1, Raspberry_Pi_1.GPIO3
  N7: Raspberry_Pi_1.ID_SD, 4_Channel_Relay2.IN2
  N8: Raspberry_Pi_1.GIPO7, 4_Channel_Relay2.IN3
  N9: Raspberry_Pi_1.GIPO8, 4_Channel_Relay2.IN4
  N10: Raspberry_Pi_1.GIPO24, 4_Channel_Relay2.IN1
  N11: Raspberry_Pi_1.GIPO23, 4_Channel_Relay1.IN4
  N12: Raspberry_Pi_1.GIPO18, 4_Channel_Relay1.IN2
  N13: Raspberry_Pi_1.GIPO15, 4_Channel_Relay1.IN1
  VCC: Raspberry_Pi_1.5V, 4_Channel_Relay1.VCC, 4_Channel_Relay2.VCC
  12V: 4_Channel_Relay1.COM, 4_Channel_Relay2.COM
  N14: 4_Channel_Relay1.NO#18, D1.anode
  N15: 4_Channel_Relay1.NO#21, D2.anode
  N16: 4_Channel_Relay1.NO#27, D3.anode
  N17: 4_Channel_Relay2.NO#18, D4.anode
  N18: 4_Channel_Relay2.NO#21, D5.anode
  N19: 4_Channel_Relay2.NO#24, D6.anode
  N20: 4_Channel_Relay2.NO#27, D7.anode
  GND_2: D1.cathode, D2.cathode, D3.cathode, D4.cathode, D5.cathode, D6.cathode, D7.cathode

custom parts:
  4 Channel Power Relay: A 4 channel power relay. The module operates at 5V.
